# Fritzing sketch feather 2 leds (saved by Fritzing 0.9.0b)
breadboards: 1

parts:
  Part1 = Adafruit Feather HUZZAH ESP8266 [part_number="Adafruit #2821"]
  LED1 = smd LED [color="White (8000K)" package="1206 [SMD]"]
  LED2 = smd LED [color="White (8000K)" package="1206 [SMD]"]

nets:
  N1: Part1.GPIO12/MISO, LED1.anode
  N2: Part1.GPIO13/MOSI, LED2.anode
  N3: Part1.GND, LED1.cathode, LED2.cathode

custom parts:
  Adafruit Feather HUZZAH ESP8266: his is the Adafruit Feather HUZZAH ESP8266 - our take on an 'all-in-one' ESP8266 WiFi development board with built in USB and battery charging. Its an ESP8266 WiFi module with all the extras you need, ready to rock! We have other boards in the Feather family, check'em out here. At the Feather HUZZAH's heart is an ESP8266 WiFi microcontroller clocked at 80 MHz and at 3.3V logic. This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
